# Fritzing sketch rpiclock (saved by Fritzing 0.9.4)

parts:
  Part4 = Seven-Segment LED Backpack 1.2 Inch Digits [part_number=1270]
  MCU1 = Raspberry Pi Zero

nets:
  N1: Part4.SCL, MCU1.pin_5
  N2: Part4.SDA, MCU1.pin_3
  N3: Part4.GND, MCU1.pin_6, MCU1.pin_9
  N4: Part4.VDD, MCU1.pin_2, MCU1.pin_4
  N5: Part4.VCCIO, MCU1.pin_1

custom parts:
  Seven-Segment LED Backpack 1.2 Inch Digits: This jumbo 1.2" 7-segment LED display includes a driver chip for simple control via an I2C interface. The backpack features address-selection jumpers so you can connect up to eight displays on a single I2C bus.
